# Fritzing sketch sketch (saved by Fritzing 0.9.3b)
breadboards: 1

parts:
  Part1 = Arduino Uno (Rev3) - ICSP
  RE1 = Rotary Encoder [package=THT]
  RE2 = Rotary Encoder [package=THT]
  U2 = SWITCH_SPDT [package=kps-1290]
  U3 = SWITCH_SPDT [package=kps-1290]
  U4 = SWITCH_SPDT [package=kps-1290]
  U5 = SWITCH_SPDT [package=kps-1290]

nets:
  N1: Part1.A0, U2.S
  N2: Part1.A1, U4.S
  N3: Part1.A2, U3.S
  N4: Part1.A3, U5.S
  N5: Part1.5V, U2.O, U3.O, U4.O, U5.O
  N6: Part1.D0/RX, RE2.EncoderPinA
  N7: Part1.D1/TX, RE2.EncoderPinC
  N8: Part1.D2, RE1.EncoderPinC
  N9: Part1.D3_PWM, RE1.EncoderPinA
  N10: Part1.GND, RE1.EncoderPinB, RE2.EncoderPinB

notes:
  load
